// Logisim project DD ASSIGNMENT.circ as structural Verilog: 1 circuit, main circuit main
module main (
  input  SENSOR,
  output Q2,
  output Q1,
  output Q0
);

  wire and_1_out, and_2_out, and_3_out, and_4_out, and_5_out, and_6_out, and_7_out, and_8_out, and_9_out,
       and_10_out, clock_1_out, d_ff_1_qn, d_ff_2_qn, d_ff_3_qn, nand_1_out, nand_2_out, nand_3_out,
       nand_4_out, or_1_out, or_2_out, or_3_out, or_4_out, or_5_out, or_6_out;

  nand nand_1 (nand_1_out, SENSOR, SENSOR);
  and and_1 (and_1_out, Q2, d_ff_2_qn);
  and and_2 (and_2_out, Q1, Q0);
  and and_3 (and_3_out, d_ff_2_qn, Q0);
  and and_4 (and_4_out, d_ff_3_qn, SENSOR);
  or or_1 (or_1_out, d_ff_1_qn, d_ff_2_qn);
  and and_5 (and_5_out, d_ff_1_qn, d_ff_2_qn);
  and and_6 (and_6_out, d_ff_1_qn, d_ff_3_qn);
  nand nand_2 (nand_2_out, Q1, Q2);
  nand nand_3 (nand_3_out, Q1, Q0);
  and and_7 (and_7_out, Q1, and_6_out);
  and and_8 (and_8_out, Q0, and_5_out);
  and and_9 (and_9_out, and_1_out, nand_1_out);
  and and_10 (and_10_out, and_4_out, or_1_out);
  or or_2 (or_2_out, and_3_out, and_7_out);
  or or_3 (or_3_out, and_1_out, and_2_out);
  or or_4 (or_4_out, or_2_out, and_9_out);
  or or_5 (or_5_out, and_8_out, and_10_out);
  or or_6 (or_6_out, and_5_out, and_6_out);
  nand nand_4 (nand_4_out, nand_2_out, nand_3_out);
  Clock clock_1 (.out(clock_1_out));
  D_Flip_Flop d_ff_1 (.clk(clock_1_out), .D(or_3_out), .Q(Q2), .Qn(d_ff_1_qn));  // open: preset, en, reset
  D_Flip_Flop d_ff_2 (.clk(clock_1_out), .D(or_4_out), .Q(Q1), .Qn(d_ff_2_qn));  // open: preset, en, reset
  D_Flip_Flop d_ff_3 (.clk(clock_1_out), .D(or_5_out), .Q(Q0), .Qn(d_ff_3_qn));  // open: preset, en, reset
  LED HG (.in(or_6_out));
  LED HY (.in(nand_4_out));
  LED HR (.in(and_1_out));
  LED SG (.in(and_1_out));
  LED SY (.in(nand_4_out));
  LED SR (.in(or_6_out));
endmodule
